// Logisim project Ejercicio1a.circ as structural Verilog: 1 circuit, main circuit main
module main (
  input  x,
  input  y,
  output x_prime_y
);

  wire not_1_out;

  not not_1 (not_1_out, x);
  or or_1 (x_prime_y, not_1_out, y);

  // Notes on the sheet:
  //   x̄ 
endmodule
