// Logisim project Ejercicio1b.circ as structural Verilog: 1 circuit, main circuit main
// x + ȳ
module main (
  input  x,
  input  y,
  output x_prime___y__x___y_prime
);

  wire not_1_out, not_2_out, or_1_out, or_2_out;

  not not_1 (not_1_out, x);
  not not_2 (not_2_out, y);
  or or_1 (or_1_out, not_1_out, y);
  or or_2 (or_2_out, x, not_2_out);
  and and_1 (x_prime___y__x___y_prime, or_1_out, or_2_out);

  // Notes on the sheet:
  //   x̄
  //   ȳ
  //   x̄ + y
  //   x + ȳ
endmodule
