// Logisim project Ejercicio1c.circ as structural Verilog: 1 circuit, main circuit main
module main (
  input  x,
  input  y,
  output n_xy__x_y
);

  wire and_1_out, not_1_out, or_1_out;

  and and_1 (and_1_out, x, y);
  or or_1 (or_1_out, x, y);
  not not_1 (not_1_out, and_1_out);
  and and_2 (n_xy__x_y, not_1_out, or_1_out);

  // Notes on the sheet:
  //   xy
  //   x + y
  //   ¬(xy)
endmodule
