// Logisim project Ejercicio2a.circ as structural Verilog: 1 circuit, main circuit main
module main (
  input  x,
  input  y,
  output x_prime_y___xy_prime___xy
);

  wire and_1_out, and_2_out, and_3_out, not_1_out, not_2_out, or_1_out;

  not not_1 (not_1_out, x);
  not not_2 (not_2_out, y);
  and and_1 (and_1_out, y, x);
  and and_2 (and_2_out, not_1_out, y);
  and and_3 (and_3_out, x, not_2_out);
  or or_1 (or_1_out, and_3_out, and_1_out);
  or or_2 (x_prime_y___xy_prime___xy, and_2_out, or_1_out);

  // Notes on the sheet:
  //   x̄ 
  //    ȳ
  //   xy
  //   x̄y 
  //   xȳ
  //   xȳ + xy
endmodule
