// Logisim project Ejercicio2b.circ as structural Verilog: 1 circuit, main circuit main
module main (
  input  x,
  input  y,
  input  z,
  output xz___yz_prime__x_prime_yz
);

  wire and_1_out, and_2_out, and_3_out, not_1_out, not_2_out, or_1_out;

  not not_1 (not_1_out, x);
  not not_2 (not_2_out, z);
  and and_1 (and_1_out, x, z);
  and and_2 (and_2_out, y, not_2_out);
  and and_3 (and_3_out, not_1_out, y, z);
  or or_1 (or_1_out, and_1_out, and_2_out);
  or or_2 (xz___yz_prime__x_prime_yz, or_1_out, and_3_out);

  // Notes on the sheet:
  //   x̄ 
  //   z̄ 
  //   xz
  //   yz̄ 
  //   x̄yz
  //   xz + yz̄ 
endmodule
