// Logisim project Ejercicio2c.circ as structural Verilog: 1 circuit, main circuit main
module main (
  input  x,
  input  y,
  input  z,
  output x__y_prime___z__x_prime___y___z_prime
);

  wire not_1_out, not_2_out, not_3_out, or_1_out, or_2_out, or_3_out, or_4_out;

  not not_1 (not_1_out, x);
  not not_2 (not_2_out, y);
  not not_3 (not_3_out, z);
  or or_1 (or_1_out, x, not_2_out);
  or or_2 (or_2_out, not_1_out, y);
  or or_3 (or_3_out, or_1_out, z);
  or or_4 (or_4_out, or_2_out, not_3_out);
  and and_1 (x__y_prime___z__x_prime___y___z_prime, or_3_out, or_4_out);

  // Notes on the sheet:
  //   x̄ 
  //    ȳ
  //   z̄ 
  //   x + ȳ
  //   x̄ + y
  //   x + ȳ + z
  //   x̄ + y + z̄ 
endmodule
