// Logisim project Ejercicio2d.circ as structural Verilog: 1 circuit, main circuit main
module main (
  input  w,
  input  x,
  input  y,
  input  z,
  output x__yz____x_prime_y_prime____zw_prime
);

  wire and_1_out, and_2_out, and_3_out, and_4_out, not_1_out, not_2_out, not_3_out, or_1_out;

  not not_1 (not_1_out, w);
  not not_2 (not_2_out, x);
  not not_3 (not_3_out, y);
  and and_1 (and_1_out, z, not_1_out);
  and and_2 (and_2_out, not_2_out, not_3_out);
  and and_3 (and_3_out, y, z);
  or or_1 (or_1_out, and_2_out, and_1_out);
  and and_4 (and_4_out, x, and_3_out);
  and and_5 (x__yz____x_prime_y_prime____zw_prime, and_4_out, or_1_out);

  // Notes on the sheet:
  //   w̄
  //   x̄ 
  //    ȳ
  //   zw̄
  //   x̄ȳ
  //   yz
  //   (x(yz))
  //   ((x̄ȳ) + (zw̄))
endmodule
