// Logisim project Ejercicio3a.circ as structural Verilog: 1 circuit, main circuit main
module main (
  input  A,
  input  B,
  input  C,
  input  D,
  input  E,
  output out_6
);

  wire _1_out, _2_out, _3_out, _4_out, _5_out, _6_out, _7_out, _8_out, _9_out, _10_out, _11_out, _12_out,
       _13_out, _14_out, _15_out, _16_out, not_1_out, not_2_out, not_3_out, not_4_out, not_5_out;

  not not_1 (not_1_out, A);
  not not_2 (not_2_out, B);
  not not_3 (not_3_out, C);
  not not_4 (not_4_out, D);
  not not_5 (not_5_out, E);
  and _1 (_1_out, not_1_out, not_2_out, C, D, E);
  and _2 (_2_out, not_1_out, B, not_3_out, D, E);
  and _3 (_3_out, not_1_out, B, C, not_4_out, E);
  and _4 (_4_out, not_1_out, B, C, D, not_5_out);
  and _5 (_5_out, not_1_out, B, C, D, E);
  and _6 (_6_out, A, not_2_out, not_3_out, D, E);
  and _7 (_7_out, A, not_2_out, C, not_4_out, E);
  and _8 (_8_out, A, not_2_out, C, D, not_5_out);
  and _9 (_9_out, A, not_2_out, C, D, E);
  and _10 (_10_out, A, B, not_3_out, not_4_out, E);
  and _11 (_11_out, A, B, not_3_out, D, not_5_out);
  and _12 (_12_out, A, B, not_3_out, D, E);
  and _13 (_13_out, A, B, C, not_4_out, not_5_out);
  and _14 (_14_out, A, B, C, not_4_out, E);
  and _15 (_15_out, A, B, C, D, not_5_out);
  and _16 (_16_out, A, B, C, D, E);
  or or_1 (out_6, _1_out, _2_out, _3_out, _4_out, _5_out, _6_out, _7_out, _8_out, _9_out, _10_out, _11_out, _12_out, _13_out, _14_out, _15_out, _16_out);

  // Notes on the sheet:
  //   ĀB̄CDE
  //   ĀBC̄DE
  //   ĀBCD̄E
  //   ĀBCDĒ
  //   AB̄CDE
  //   ĀBCDE
  //   AB̄C̄DE
  //   AB̄CD̄E
  //   AB̄CDĒ
  //   ABC̄D̄E
  //   ABC̄DĒ
  //   ABC̄DE
  //   ABCD̄Ē 
  //   ABCD̄E
  //   ABCDĒ 
  //   ABCDE
  //   ĀB̄CDE + ĀBC̄DE + ĀBCD̄E + ĀBCDĒ + ĀBCDE + AB̄C̄DE + AB̄CD̄E + AB̄CDĒ + AB̄CDE + ABC̄D̄E + ABC̄DĒ + ABC̄DE + ABCD̄Ē + ABCD̄E + ABCDĒ + ABCDE
endmodule
