// Logisim project Ejercicio3b.circ as structural Verilog: 1 circuit, main circuit main
module main (
  input  x,
  input  y,
  input  z,
  output x_prime_y_prime_z___x_prime_yz_prime___xy_prime_z_prime____xyz
);

  wire and_1_out, and_2_out, and_3_out, and_4_out, and_5_out, and_6_out, and_7_out, and_8_out, not_1_out,
       not_2_out, not_3_out, or_1_out, or_3_out;

  not not_1 (not_1_out, x);
  not not_2 (not_2_out, y);
  not not_3 (not_3_out, z);
  and and_1 (and_1_out, not_1_out, not_2_out);
  and and_2 (and_2_out, x, y);
  and and_3 (and_3_out, and_1_out, z);
  and and_4 (and_4_out, and_2_out, z);
  and and_5 (and_5_out, not_1_out, y);
  and and_6 (and_6_out, and_5_out, not_3_out);
  and and_7 (and_7_out, x, not_2_out);
  and and_8 (and_8_out, and_7_out, not_3_out);
  or or_1 (or_1_out, and_3_out, and_6_out);
  or or_2 (x_prime_y_prime_z___x_prime_yz_prime___xy_prime_z_prime____xyz, or_1_out, or_3_out);
  or or_3 (or_3_out, and_8_out, and_4_out);

  // Notes on the sheet:
  //   Circuito inciso b ejercicio 3 
  //   x̄ 
  //    ȳ
  //   z̄ 
  //   x̄ȳ
  //   xy 
  //   x̄ȳz
  //   x̄y
  //   xȳ 
  //   xyz 
  //   x̄yz̄ 
  //   xȳz̄  
  //   x̄ȳz + x̄yz̄ 
  //   xȳz̄  + xyz
endmodule
