// Logisim project Ejercicio3c.circ as structural Verilog: 1 circuit, main circuit main
module main (
  input  X,
  input  Y,
  output x_prime_y___xy_prime___xy
);

  wire and_1_out, and_2_out, and_3_out, not_1_out, not_2_out, or_1_out;

  not not_1 (not_1_out, X);
  not not_2 (not_2_out, Y);
  and and_1 (and_1_out, not_1_out, Y);
  and and_2 (and_2_out, X, not_2_out);
  and and_3 (and_3_out, X, Y);
  or or_1 (or_1_out, and_1_out, and_2_out);
  or or_2 (x_prime_y___xy_prime___xy, or_1_out, and_3_out);

  // Notes on the sheet:
  //   x̄ 
  //    ȳ
  //   x̄y
  //    xȳ
  //   xy
  //   x̄y + xȳ
endmodule
