// Logisim project contador3.circ as structural Verilog: 1 circuit, main circuit main
module main (
  output Q2,
  output Q1,
  output Q0
);

  wire and_1_out, clock_1_out;

  Clock clock_1 (.out(clock_1_out));
  T_Flip_Flop #(.NewFFLayout("false")) t_ff_1 (.clk(clock_1_out), .T(1'b1), .Q(Q0));  // open: Qn, preset, reset
  T_Flip_Flop #(.NewFFLayout("false")) t_ff_2 (.clk(clock_1_out), .T(Q0), .Q(Q1));  // open: Qn, preset, reset
  and and_1 (and_1_out, Q1, Q0);
  T_Flip_Flop #(.NewFFLayout("false")) t_ff_3 (.clk(clock_1_out), .T(and_1_out), .Q(Q2));  // open: Qn, preset, reset
endmodule
